# Fritzing sketch Esquematico_rampa (saved by Fritzing 0.9.2b)
breadboards: 1

parts:
  Componente1 = Arduino Mega 2560 (Rev3)
  R14 = Photocell (LDR) [package=THT]
  R15 = Resistor [tolerance=±5% resistance=10k package=THT]
  R16 = Resistor [tolerance=±5% resistance=10k package=THT]
  R17 = Resistor [tolerance=±5% resistance=10k package=THT]
  R18 = Resistor [tolerance=±5% resistance=10k package=THT]
  R19 = Resistor [tolerance=±5% resistance=10k package=THT]
  R20 = Resistor [tolerance=±5% resistance=10k package=THT]
  R21 = Resistor [tolerance=±5% resistance=10k package=THT]
  R22 = Resistor [tolerance=±5% resistance=10k package=THT]
  R23 = Photocell (LDR) [package=THT]
  R24 = Photocell (LDR) [package=THT]
  R25 = Photocell (LDR) [package=THT]
  R26 = Photocell (LDR) [package=THT]
  R27 = Photocell (LDR) [package=THT]
  R28 = Photocell (LDR) [package=THT]
  R29 = Photocell (LDR) [package=THT]
  R30 = Photocell (LDR) [package=THT]
  R31 = Resistor [tolerance=±5% resistance=10k package=THT]
  R32 = Photocell (LDR) [package=THT]
  R33 = Resistor [tolerance=±5% resistance=10k package=THT]
  R34 = Photocell (LDR) [package=THT]
  R35 = Resistor [tolerance=±5% resistance=10k package=THT]

nets:
  N1: Componente1.A8, R16.Pin_1, R23.pin_0
  N2: Componente1.A9, R14.pin_0, R20.Pin_1
  N3: Componente1.A10, R34.pin_0, R35.Pin_1
  N4: Componente1.A0, R30.pin_0, R31.Pin_1
  N5: Componente1.A1, R32.pin_0, R33.Pin_1
  N6: Componente1.A2, R22.Pin_1, R29.pin_0
  N7: Componente1.A3, R21.Pin_1, R28.pin_0
  N8: Componente1.A4, R18.Pin_1, R27.pin_0
  N9: Componente1.A5, R17.Pin_1, R26.pin_0
  N10: Componente1.A6, R15.Pin_1, R25.pin_0
  N11: Componente1.A7, R19.Pin_1, R24.pin_0
  N12: Componente1.5V, R15.Pin_0, R16.Pin_0, R17.Pin_0, R18.Pin_0, R19.Pin_0, R20.Pin_0, R21.Pin_0, R22.Pin_0, R31.Pin_0, R33.Pin_0, R35.Pin_0
  N13: Componente1.GND, R14.pin_1, R23.pin_1, R24.pin_1, R25.pin_1, R26.pin_1, R27.pin_1, R28.pin_1, R29.pin_1, R30.pin_1, R32.pin_1, R34.pin_1
